# Fritzing sketch week-1 (saved by Fritzing 0.9.2b)
breadboards: 1

parts:
  R1 = Resistor [tolerance=±5% resistance=220 package=THT]
  LED1 = LED - 5mm [color="Red (633nm)" package="5 mm [THT]"]
  Raspberry_Pi1 = Raspberry Pi B+

nets:
  N1: R1.Pin_0, LED1.anode
  N2: R1.Pin_1, LED1.cathode, Raspberry_Pi1.GIPO13, Raspberry_Pi1.GND, Raspberry_Pi1.GIPO21
