# Fritzing sketch week-3 (saved by Fritzing 0.9.2b)
breadboards: 1

parts:
  Parte1 = Arduino Uno (Rev3) - ICSP
  T1 = TMP36 Temperature Sensor [package="TO92 [THT]"]
  Raspberry_Pi1 = Raspberry Pi B+  # not connected

nets:
  N1: Parte1.A0, T1.Vout
  N2: Parte1.5V, T1.+Vs
  GND: Parte1.GND, T1.GND
