# Fritzing sketch week-4 (saved by Fritzing 0.9.2b)
breadboards: 1

parts:
  DHT1 = DHT11 Humitidy and Temperature Sensor
  Raspberry_Pi1 = Raspberry Pi B+

nets:
  VDD: DHT1.VDD, Raspberry_Pi1.5V
  N1: DHT1.DATA, Raspberry_Pi1.GIPO15
  GND: DHT1.GND, Raspberry_Pi1.GND

custom parts:
  DHT11 Humitidy and Temperature Sensor: DHT11 Humidity and Temperature Sensor
